# Fritzing sketch Full Schematic - Binary Clock (saved by Fritzing 0.9.2b)
breadboards: 1

parts:
  Part1 = Arduino Uno (Rev3) - ICSP
  S1 = Pushbutton [package="[THT]"]
  S2 = Pushbutton [package="[THT]"]
  S3 = Pushbutton [package="[THT]"]
  U1 = 74HC595 SMD [package="SO16 [SMD]"]

nets:
  N1: Part1.A0, S3.Pin_3, S3.Pin_4
  N2: Part1.A1, U1.ST_CP
  N3: Part1.A2, U1.SH_CP
  N4: Part1.A3, U1.DS
  N5: Part1.A4/SDA, S2.Pin_3, S2.Pin_4
  N6: Part1.A5/SCL, S1.Pin_3, S1.Pin_4
  GND: Part1.GND, U1.GND, U1.OE
  5V: Part1.5V, U1.MR, U1.VCC
  N7: S1.Pin_1, S1.Pin_2, S2.Pin_1, S2.Pin_2, S3.Pin_1, S3.Pin_2

notes:
  To LED 12 - BTM Right (white power cable)
  To LED 13 on Cardboard - continue pattern downwards
  To Ground of all day of the week LED's
  To Power of of Monday, then pin1 on 74H is tuesday etc.
